# Fritzing sketch schematic (saved by Fritzing 0.9.3b)

parts:
  microSD1 = MicroSD Card Module
  U1 = GP-2106 [package=gp-2106]
  Part1 = Arduino Uno (Rev3)
  LED1 = Super Flux LED blue [color=Blue]

nets:
  GND: microSD1.GND, U1.GND, Part1.GND, LED1.anode
  VCC: microSD1.VCC, U1.VCC, Part1.5V
  N1: microSD1.MISO, Part1.D12/MISO
  N2: microSD1.MOSI, Part1.D11_PWM/MOSI
  N3: microSD1.SCK, Part1.D13/SCK
  N4: microSD1.CS, Part1.D8
  N5: U1.RX, Part1.D4
  N6: U1.TX, Part1.D3_PWM
  N7: Part1.D2, LED1.cathode
